// Logisim project cpu.circ as structural Verilog: 2 circuits, main circuit main
module main (
  input  [31:0] INSTRUCTION,
  input  CLOCK,
  output [31:0] FETCH_ADDRESS,
  output [31:0] s0_Value,
  output [31:0] s1_Value,
  output [31:0] t0_Value,
  output [31:0] t1_Value,
  output [31:0] a0_Value,
  output [31:0] ra_Value,
  output [31:0] sp_Value
);

  wire ASel, BSel, Control_Unit_addtype, Control_Unit_andtype, Control_Unit_divtype, Control_Unit_mulhtype,
       Control_Unit_multype, Control_Unit_ortype, Control_Unit_remtype, Control_Unit_slltype,
       Control_Unit_slttype, Control_Unit_srltype, Control_Unit_subtype, Control_Unit_xortype, MEM_p1,
       MEM_p2, MEM_p4, MEM_p10, MemRW, PCSel, RegWEn;
  wire [1:0] WBSel;
  wire [2:0] ImmSel;
  wire [3:0] ALUSel;
  wire [24:0] demultiplexer_1_out1, Iimm, SBimm, Simm, Uimm, UJimm;
  wire [24:13] iImm_t;
  wire [31:0] adder_1_out, bit_extender_1_out, bit_extender_2_out, bit_extender_3_out, bit_extender_4_out,
       immGen, main_1_read_data_1, main_1_read_data_2, main_2_result, MEM_p11, multiplexer_1_out,
       multiplexer_3_out, multiplexer_4_out, multiplexer_5_out;

  Multiplexer #(.width(32)) multiplexer_1 (
    .in0(adder_1_out), .in1(main_2_result), .out(multiplexer_1_out), .sel(PCSel));  // open: en
  Register #(.width(32)) PC (.D(multiplexer_1_out), .Q(FETCH_ADDRESS), .clk(CLOCK));  // open: en, clr
  Adder #(.width(32)) adder_1 (.a(FETCH_ADDRESS), .b(32'h4), .out(adder_1_out));  // open: cin, cout
  assign bit_extender_1_out = {{20{1'b0}}, iImm_t};  // Bit_Extender bit_extender_1
  assign bit_extender_2_out = {{20{1'b0}}, {Simm[24:18], Simm[4:0]}};  // Bit_Extender bit_extender_2
  assign bit_extender_3_out = {{19{1'b0}}, {SBimm[24], SBimm[0], SBimm[23:18], SBimm[4:1], 1'b0}};  // Bit_Extender bit_extender_3
  assign bit_extender_4_out = {{11{1'b0}}, {UJimm[24], UJimm[12:5], UJimm[13], UJimm[23:14], 1'b0}};  // Bit_Extender bit_extender_4
  Demultiplexer #(.select(3), .width(25)) demultiplexer_1 (
    .out0(Iimm), .out1(demultiplexer_1_out1), .out2(SBimm), .out3(Uimm), .out4(UJimm),
    .in(INSTRUCTION[31:7]), .sel(ImmSel));  // open: out5, out6, out7, en
  Multiplexer #(.select(3), .width(32)) multiplexer_2 (
    .in0(bit_extender_1_out), .in1(bit_extender_2_out), .in2(bit_extender_3_out),
    .in3({Uimm[24:5], {12{1'b0}}}), .in4(bit_extender_4_out), .out(immGen), .sel(ImmSel));  // open: in5, in6, in7, en
  regfile_main main_1 (
    .Read_Register_1__rs1(INSTRUCTION[19:15]), .Read_Register_2__rs2(INSTRUCTION[24:20]),
    .Write_Register__rd(INSTRUCTION[11:7]), .Write_Data(multiplexer_5_out), .Write_Enable(RegWEn),
    .Clock(CLOCK), .Read_Data_1(main_1_read_data_1), .Read_Data_2(main_1_read_data_2), .s1_Value(s1_Value),
    .t0_Value(t0_Value), .t1_Value(t1_Value), .a0_Value(a0_Value), .s0_Value(s0_Value), .ra_Value(ra_Value),
    .sp_Value(sp_Value));
  not not_1 (PCSel, RegWEn);
  or or_1 (RegWEn, Control_Unit_addtype, Control_Unit_multype, Control_Unit_subtype, Control_Unit_slltype, Control_Unit_mulhtype, Control_Unit_slttype, Control_Unit_xortype, Control_Unit_divtype, Control_Unit_srltype, Control_Unit_ortype, Control_Unit_remtype, Control_Unit_andtype);
  not not_2 (ASel, RegWEn);
  not not_3 (BSel, RegWEn);
  Multiplexer #(.width(32)) multiplexer_3 (
    .in0(main_1_read_data_2), .in1(immGen), .out(multiplexer_3_out), .sel(BSel));  // open: en
  not not_4 (MemRW, RegWEn);
  Multiplexer #(.width(32)) multiplexer_4 (
    .in0(main_1_read_data_1), .in1(adder_1_out), .out(multiplexer_4_out), .sel(ASel));  // open: en
  control_unit Control_Unit (
    .Instruction(INSTRUCTION), .ANDtype(Control_Unit_andtype), .REMtype(Control_Unit_remtype),
    .ORtype(Control_Unit_ortype), .SRLtype(Control_Unit_srltype), .DIVtype(Control_Unit_divtype),
    .XORtype(Control_Unit_xortype), .SLTtype(Control_Unit_slttype), .MULHtype(Control_Unit_mulhtype),
    .SLLtype(Control_Unit_slltype), .SUBtype(Control_Unit_subtype), .MULtype(Control_Unit_multype),
    .ADDtype(Control_Unit_addtype));  // open: JALRtype, JALtype, LUItype, BLTUtype, BLTtype, BEQtype, SWtype, ANDItype, ORItype, SRLItype, XORItype, SLTItype, SLLItype, ADDItype, LWtype, LHtype, LBtype
  alu_main main_2 (
    .Switch(ALUSel), .X(multiplexer_4_out), .Result(main_2_result), .Y(multiplexer_3_out));  // open: Equal
  // mem_main MEM: pin names not known; wires that end beside it: MEM_p1, MEM_p2, MEM_p2, MEM_p4, main_2_result, main_1_read_data_2, MemRW, MEM_p4, CLOCK, MEM_p10, MEM_p11
  Multiplexer #(.select(2), .width(32)) multiplexer_5 (
    .in0(adder_1_out), .in1(main_2_result), .in2(MEM_p11), .out(multiplexer_5_out), .sel(WBSel));  // open: in3, en

  // Other names for the same wires on the sheet: a0[31:0] = a0_Value; clk = CLOCK; fetch_addr[31:0] = FETCH_ADDRESS;
  //   ra[31:0] = ra_Value; s0[31:0] = s0_Value; s1[31:0] = s1_Value; sp[31:0] = sp_Value; t0[31:0] = t0_Value;
  //   t1[31:0] = t1_Value

  // Notes on the sheet:
  //   Output
  //   These are outputs/inputs from run.circ
  //   Inputs
  //   These are DEBUG/TEST outputs from your circuit.
endmodule

module control_unit (
  input  [31:0] Instruction,
  output JALRtype,
  output JALtype,
  output LUItype,
  output BLTUtype,
  output BLTtype,
  output BEQtype,
  output SWtype,
  output ANDItype,
  output ORItype,
  output SRLItype,
  output XORItype,
  output SLTItype,
  output SLLItype,
  output ADDItype,
  output LWtype,
  output LHtype,
  output LBtype,
  output ANDtype,
  output REMtype,
  output ORtype,
  output SRLtype,
  output DIVtype,
  output XORtype,
  output SLTtype,
  output MULHtype,
  output SLLtype,
  output SUBtype,
  output MULtype,
  output ADDtype
);

  wire demultiplexer_1_out0, demultiplexer_1_out1, demultiplexer_2_out0, demultiplexer_4_out0,
       demultiplexer_4_out1, demultiplexer_5_out1, demultiplexer_6_out0, demultiplexer_8_out1,
       demultiplexer_10_out0, demultiplexer_10_out1, demultiplexer_11_out0, demultiplexer_11_out1,
       demultiplexer_12_out0, demultiplexer_12_out1, demultiplexer_15_out0, demultiplexer_15_out1,
       demultiplexer_16_out0, demultiplexer_16_out1, demultiplexer_17_out0, demultiplexer_17_out1,
       demultiplexer_19_out0, demultiplexer_20_out0, demultiplexer_20_out1, demultiplexer_21_out0,
       demultiplexer_21_out1, demultiplexer_22_out0, demultiplexer_22_out1, demultiplexer_23_out0,
       demultiplexer_23_out1, demultiplexer_25_out0, Itype, LoadItype, Rtype;

  Demultiplexer demultiplexer_1 (
    .out0(demultiplexer_1_out0), .out1(demultiplexer_1_out1), .in(1'b1), .sel(Instruction[6]));  // open: en
  Demultiplexer demultiplexer_2 (
    .out0(demultiplexer_2_out0), .out1(JALtype), .in(demultiplexer_1_out1), .sel(Instruction[3]));  // open: en
  Demultiplexer demultiplexer_3 (
    .out0(LoadItype), .out1(Itype), .in(demultiplexer_4_out0), .sel(Instruction[3]));  // open: en
  Demultiplexer demultiplexer_4 (
    .out0(demultiplexer_4_out0), .out1(demultiplexer_4_out1), .in(demultiplexer_1_out0), .sel(Instruction[5]));  // open: en
  Demultiplexer demultiplexer_5 (
    .out0(SWtype), .out1(demultiplexer_5_out1), .in(demultiplexer_4_out1), .sel(Instruction[4]));  // open: en
  Demultiplexer demultiplexer_6 (
    .out0(demultiplexer_6_out0), .out1(JALRtype), .in(demultiplexer_2_out0), .sel(Instruction[2]));  // open: en
  Demultiplexer demultiplexer_7 (
    .out0(Rtype), .out1(LUItype), .in(demultiplexer_5_out1), .sel(Instruction[2]));  // open: en
  Demultiplexer demultiplexer_8 (
    .out0(BEQtype), .out1(demultiplexer_8_out1), .in(demultiplexer_6_out0), .sel(Instruction[14]));  // open: en
  Demultiplexer demultiplexer_9 (
    .out0(BLTtype), .out1(BLTUtype), .in(demultiplexer_8_out1), .sel(Instruction[13]));  // open: en
  Demultiplexer demultiplexer_10 (
    .out0(demultiplexer_10_out0), .out1(demultiplexer_10_out1), .in(demultiplexer_11_out0),
    .sel(Instruction[13]));  // open: en
  Demultiplexer demultiplexer_11 (
    .out0(demultiplexer_11_out0), .out1(demultiplexer_11_out1), .in(Itype), .sel(Instruction[14]));  // open: en
  Demultiplexer demultiplexer_12 (
    .out0(demultiplexer_12_out0), .out1(demultiplexer_12_out1), .in(demultiplexer_11_out1),
    .sel(Instruction[13]));  // open: en
  Demultiplexer demultiplexer_13 (
    .out0(ADDItype), .out1(SLLItype), .in(demultiplexer_10_out0), .sel(Instruction[12]));  // open: en
  Demultiplexer demultiplexer_14 (
    .out0(XORItype), .out1(SRLItype), .in(demultiplexer_12_out0), .sel(Instruction[12]));  // open: en
  Demultiplexer demultiplexer_15 (
    .out0(demultiplexer_15_out0), .out1(demultiplexer_15_out1), .in(demultiplexer_16_out0),
    .sel(Instruction[13]));  // open: en
  Demultiplexer demultiplexer_16 (
    .out0(demultiplexer_16_out0), .out1(demultiplexer_16_out1), .in(Rtype), .sel(Instruction[14]));  // open: en
  Demultiplexer demultiplexer_17 (
    .out0(demultiplexer_17_out0), .out1(demultiplexer_17_out1), .in(demultiplexer_16_out1),
    .sel(Instruction[13]));  // open: en
  Demultiplexer demultiplexer_18 (
    .out0(SLTItype), .in(demultiplexer_10_out1), .sel(Instruction[12]));  // open: out1, en
  Demultiplexer demultiplexer_19 (
    .out0(demultiplexer_19_out0), .out1(LWtype), .in(LoadItype), .sel(Instruction[13]));  // open: en
  Demultiplexer demultiplexer_20 (
    .out0(demultiplexer_20_out0), .out1(demultiplexer_20_out1), .in(demultiplexer_15_out0),
    .sel(Instruction[12]));  // open: en
  Demultiplexer demultiplexer_21 (
    .out0(demultiplexer_21_out0), .out1(demultiplexer_21_out1), .in(demultiplexer_15_out1),
    .sel(Instruction[12]));  // open: en
  Demultiplexer demultiplexer_22 (
    .out0(demultiplexer_22_out0), .out1(demultiplexer_22_out1), .in(demultiplexer_17_out0),
    .sel(Instruction[12]));  // open: en
  Demultiplexer demultiplexer_23 (
    .out0(demultiplexer_23_out0), .out1(demultiplexer_23_out1), .in(demultiplexer_17_out1),
    .sel(Instruction[12]));  // open: en
  Demultiplexer demultiplexer_24 (
    .out0(ORItype), .out1(ANDItype), .in(demultiplexer_12_out1), .sel(Instruction[12]));  // open: en
  Demultiplexer demultiplexer_25 (
    .out0(demultiplexer_25_out0), .out1(SUBtype), .in(demultiplexer_20_out0), .sel(Instruction[30]));  // open: en
  Demultiplexer demultiplexer_26 (
    .out0(SLLtype), .out1(MULHtype), .in(demultiplexer_20_out1), .sel(Instruction[25]));  // open: en
  Demultiplexer demultiplexer_27 (.out0(SLTtype), .in(demultiplexer_21_out0), .sel(Instruction[25]));  // open: out1, en
  Demultiplexer demultiplexer_28 (.in(demultiplexer_21_out1), .sel(Instruction[25]));  // open: out0, out1, en
  Demultiplexer demultiplexer_29 (
    .out0(XORtype), .out1(DIVtype), .in(demultiplexer_22_out0), .sel(Instruction[25]));  // open: en
  Demultiplexer demultiplexer_30 (.out0(SRLtype), .in(demultiplexer_22_out1), .sel(Instruction[25]));  // open: out1, en
  Demultiplexer demultiplexer_31 (
    .out0(ORtype), .out1(REMtype), .in(demultiplexer_23_out0), .sel(Instruction[25]));  // open: en
  Demultiplexer demultiplexer_32 (.out0(ANDtype), .in(demultiplexer_23_out1), .sel(Instruction[25]));  // open: out1, en
  Demultiplexer demultiplexer_33 (
    .out0(LBtype), .out1(LHtype), .in(demultiplexer_19_out0), .sel(Instruction[12]));  // open: en
  Demultiplexer demultiplexer_34 (
    .out0(ADDtype), .out1(MULtype), .in(demultiplexer_25_out0), .sel(Instruction[25]));  // open: en

  // Other names for the same wires on the sheet: Op2 = Instruction[2]; Op3 = Instruction[3]; Op4 = Instruction[4];
  //   Op5 = Instruction[5]; Op6 = Instruction[6]; Func3_12 = Instruction[12]; Func3_13 = Instruction[13];
  //   Func3_14 = Instruction[14]; Func7_25 = Instruction[25]; Func7_30 = Instruction[30]

  // Notes on the sheet:
  //   ITypes
  //   UJTypes
  //   UTypes
  //   SBTypes
  //   STypes
  //   ITypes
  //   RTypes
endmodule
